# Fritzing sketch esquema-prototipo-nodemcu (saved by Fritzing 0.9.3b)
breadboards: 1

parts:
  U1 = NodeMCU V3.0
  hc-sr1 = hc-sr04
  Part1 = KY-016 RGB Full Color LED Module [package="Breakout board"]
  Componente1 = Arduino Nano (Rev3.0)

nets:
  N1: U1.D1, hc-sr1.Echo
  N2: U1.D2, hc-sr1.Trig
  N3: U1.GND#6, U1.GND#13, U1.GND#16, U1.GND#33, hc-sr1.GND, Part1.-
  N4: U1.D5, Part1.R
  N5: U1.D6, Part1.G
  N6: U1.D7, Part1.B
  VCC: hc-sr1.VCC, Componente1.5V

custom parts:
  NodeMCU V3.0: ESP8266 based NodeMCU
  KY-016 RGB Full Color LED Module: KY-016 Arduino full color 5mm RGB LED, different colors can be obtained by mixing the three primary colors.
